// Logisim project Interface_lb_reptar.circ as structural Verilog: 4 circuits, main circuit FPGA_Top
module FPGA_Top (
);

  wire clk, clk_pll_200_1_p1, clk_pll_200_1_p2, lba_ctrl_1_p9, lba_ctrl_1_p10, lba_ctrl_1_p11,
       lba_ctrl_1_p12, lba_ctrl_1_p13, lba_ctrl_1_p15, lba_ctrl_1_p16, lba_ctrl_1_p17, nReset, reptarlb_1_p1,
       reptarlb_1_p2, reptarlb_1_p3, reptarlb_1_p4, reptarlb_1_p5, reptarlb_1_p8, reptarlb_1_p9,
       reptarlb_1_p10, Reset;
  wire [7:0] aff_7seg_1, Leds, Switchs;
  wire [15:0] l_lba_user_interface_data_rd_o, lba_std_interface_p10, reptarlb_1_p6, reptarlb_1_p7;
  wire [22:0] lba_ctrl_1_p14;

  Button SW_reset (.out(Reset));
  // ReptarLB reptarlb_1: pin names not known; wires that end beside it: reptarlb_1_p1, reptarlb_1_p2, reptarlb_1_p3, reptarlb_1_p4, reptarlb_1_p5, reptarlb_1_p6, reptarlb_1_p7, reptarlb_1_p8, reptarlb_1_p9, reptarlb_1_p10
  not not_1 (nReset, Reset);
  // VHDL_Entity #(.content("-- file: clk_PLL_200.vhd\n-- \n-- (c) Copyright 2008 - 2011 Xilinx, Inc. All rights reserved.\n-- \n-- This file contains confidential and proprietary information\n-- of Xilinx, Inc. and is protected under U.S. and\n-- international copyright and other intellectual property\n-- laws.\n-- \n-- DISCLAIMER\n-- This disclaimer is not a license and does not grant any\n-- rights to the materials distributed herewith. Except as\n-- otherwise provided in a valid license issued to you by\n-- Xilinx, and to the maximum extent permitted by applicable\n-- law: (1) THESE MATERIALS ARE MADE AVAILABLE \"AS IS\" AND\n-- WITH ALL FAULTS, AND XILINX HEREBY DISCLAIMS ALL WARRANTIES\n-- AND CONDITIONS, EXPRESS, IMPLIED, OR STATUTORY, INCLUDING\n-- BUT NOT LIMITED TO WARRANTIES OF MERCHANTABILITY, NON-\n-- INFRINGEMENT, OR FITNESS FOR ANY PARTICULAR PURPOSE; and\n-- (2) Xilinx shall not be liable (whether in contract or tort,\n-- including negligence, or under any other theory of\n-- liability) for any loss or damage of any kind or nature\n-- related to, arising under or in connection with these\n-- materials, including for any direct, or any indirect,\n-- special, incidental, or consequential loss or damage\n-- (including loss of data, profits, goodwill, or any type of\n-- loss or damage suffered as a result of any action brought\n-- by a third party) even if such damage or loss was\n-- reasonably foreseeable or Xilinx had been advised of the\n-- possibility of the same.\n-- \n-- CRITICAL APPLICATIONS\n-- Xilinx products are not designed or intended to be fail-\n-- safe, or for use in any application requiring fail-safe\n-- performance, such as life-support or safety devices or\n-- systems, Class III medical devices, nuclear facilities,\n-- applications related to the deployment of airbags, or any\n-- other applications that could lead to death, personal\n-- injury, or severe property or environmental damage\n-- (individually and collectively, \"Critical\n-- Applications\"). Customer assumes the sole risk and\n-- liability of any use of Xilinx products in Critical\n-- Applications, subject only to applicable laws and\n-- regulations governing limitations on product liability.\n-- \n-- THIS COPYRIGHT NOTICE AND DISCLAIMER MUST BE RETAINED AS\n-- PART OF THIS FILE AT ALL TIMES.\n-- \n------------------------------------------------------------------------------\n-- User entered comments\n------------------------------------------------------------------------------\n-- None\n--\n------------------------------------------------------------------------------\n-- \"Output    Output      Phase     Duty      Pk-to-Pk        Phase\"\n-- \"Clock    Freq (MHz) (degrees) Cycle (%) Jitter (ps)  Error (ps)\"\n------------------------------------------------------------------------------\n-- CLK_OUT1___100.000______0.000______50.0______172.490____235.738\n-- CLK_OUT2___200.000______0.000______50.0______150.969____235.738\n--\n------------------------------------------------------------------------------\n-- \"Input Clock   Freq (MHz)    Input Jitter (UI)\"\n------------------------------------------------------------------------------\n-- __primary_________100.000____________0.010\n\nlibrary ieee;\nuse ieee.std_logic_1164.all;\nuse ieee.std_logic_unsigned.all;\nuse ieee.std_logic_arith.all;\nuse ieee.numeric_std.all;\n\nlibrary unisim;\nuse unisim.vcomponents.all;\n\nentity clk_PLL_200 is\nport\n (-- Clock in ports\n  PLL_IN_i           : in     std_logic;\n  -- Clock out ports\n  PLL_100MHz_o          : out    std_logic;\n  PLL_200MHz_o          : out    std_logic;\n  -- Status and control signals\n  Reset_i             : in     std_logic;\n  locked_o            : out    std_logic\n );\nend clk_PLL_200;\n\narchitecture xilinx of clk_PLL_200 is\n  attribute CORE_GENERATION_INFO : string;\n  attribute CORE_GENERATION_INFO of xilinx : architecture is \"clk_PLL_200,clk_wiz_v3_2,{component_name=clk_PLL_200,use_phase_alignment=true,use_min_o_jitter=false,use_max_i_jitter=false,use_dyn_phase_shift=false,use_inclk_switchover=false,use_dyn_reconfig=false,feedback_source=FDBK_AUTO,primtype_sel=PLL_BASE,num_out_clk=2,clkin1_period=10.0,clkin2_period=10.0,use_power_down=false,use_reset=true,use_locked=true,use_inclk_stopped=false,use_status=false,use_freeze=false,use_clk_valid=false,feedback_type=SINGLE,clock_mgr_type=MANUAL,manual_override=false}\";\n  -- Input clock buffering / unused connectors\n  signal clkin1      : std_logic;\n  -- Output clock buffering / unused connectors\n  signal clkfbout         : std_logic;\n  signal clkfbout_buf     : std_logic;\n  signal clkout0          : std_logic;\n  signal clkout1          : std_logic;\n  signal clkout2_unused   : std_logic;\n  signal clkout3_unused   : std_logic;\n  signal clkout4_unused   : std_logic;\n  signal clkout5_unused   : std_logic;\n  -- Unused status signals\n\nbegin\n\n\n  -- Input buffering\n  --------------------------------------\n  clkin1_buf : IBUFG\n  port map\n   (O => clkin1,\n    I => PLL_IN_i);\n\n\n  -- Clocking primitive\n  --------------------------------------\n  -- Instantiation of the PLL primitive\n  --    * Unused inputs are tied off\n  --    * Unused outputs are labeled unused\n\n  pll_base_inst : PLL_BASE\n  generic map\n   (BANDWIDTH            => \"OPTIMIZED\",\n    CLK_FEEDBACK         => \"CLKFBOUT\",\n    COMPENSATION         => \"SYSTEM_SYNCHRONOUS\",\n    DIVCLK_DIVIDE        => 1,\n    CLKFBOUT_MULT        => 4,\n    CLKFBOUT_PHASE       => 0.000,\n    CLKOUT0_DIVIDE       => 4,\n    CLKOUT0_PHASE        => 0.000,\n    CLKOUT0_DUTY_CYCLE   => 0.500,\n    CLKOUT1_DIVIDE       => 2,\n    CLKOUT1_PHASE        => 0.000,\n    CLKOUT1_DUTY_CYCLE   => 0.500,\n    CLKIN_PERIOD         => 10.0,\n    REF_JITTER           => 0.010)\n  port map\n    -- Output clocks\n   (CLKFBOUT            => clkfbout,\n    CLKOUT0             => clkout0,\n    CLKOUT1             => clkout1,\n    CLKOUT2             => clkout2_unused,\n    CLKOUT3             => clkout3_unused,\n    CLKOUT4             => clkout4_unused,\n    CLKOUT5             => clkout5_unused,\n    -- Status and control signals\n    LOCKED              => locked_o,\n    RST                 => Reset_i,\n    -- Input clock control\n    CLKFBIN             => clkfbout_buf,\n    CLKIN               => clkin1);\n\n  -- Output buffering\n  -------------------------------------\n  clkf_buf : BUFG\n  port map\n   (O => clkfbout_buf,\n    I => clkfbout);\n\n\n  clkout1_buf : BUFG\n  port map\n   (O   => PLL_100MHz_o,\n    I   => clkout0);\n\n\n\n  clkout2_buf : BUFG\n  port map\n   (O   => PLL_200MHz_o,\n    I   => clkout1);\n\nend xilinx;")) clk_pll_200_1: pin names not known; wires that end beside it: clk_pll_200_1_p1, clk_pll_200_1_p2, Reset, clk
  Clock sysclk (.out(clk_pll_200_1_p1));
  Clock #(.highDuration(4), .lowDuration(4)) mainclk (.out(clk_pll_200_1_p2));
  not not_2 (reptarlb_1_p8, lba_ctrl_1_p11);
  not not_3 (reptarlb_1_p5, lba_ctrl_1_p10);
  // VHDL_Entity #(.content("-----------------------------------------------------------------------------------------------------------------------\n-- HEIG-VD ///////////////////////////////////////////////////////////////////////////////\n-- Haute Ecole d'Ingenerie et de Gestion du Canton de Vaud\n-- School of Business and Engineering in Canton de Vaud\n-----------------------------------------------------------------------------------------------------------------------\n-- REDS Institute ////////////////////////////////////////////////////////////////////////\n-- Reconfigurable Embedded Digital Systems\n-----------------------------------------------------------------------------------------------------------------------\n--\n-- File                 : lba_ctrl.vhd\n-- Author               : Evangelina Lolivier-Exler\n-- Date                 : 01.11.2013\n-- Target Devices       : Spartan6 xc6slx150t-3fgg900\n--\n-- Context              : Reptar - FPGA design\n--\n--------------------------------------------------------------------------------------------------------------------------\n-- Description :		local bus asynchronous (lba) controller  \n--						Controls the data transfers between the DM3730 and the standard or user REPTAR interfaces\n--						(lba_std_interface.vhd and lba_usr_interface.vhd)\n--						From the DM3730 side, the Local Bus is controller by the GPMC (General Purpose Memory Controller)\n--						The clock provided by the GPMC is not used in this block, that's why it is called \"asynchrounous\"\n--						The state machine of this block runs at 200 MHz (internal FPGA clock)\n--------------------------------------------------------------------------------------------------------------------------\n-- Information :\n--------------------------------------------------------------------------------------------------------------------------\n-- Modifications :\n-- Ver   Date        Engineer     Comments\n-- 0.0   See header  ELR          Initial version\n-- 1.0   03.04.2013  KGS		    Adaptation for logisim\n\n--------------------------------------------------------------------------------------------------------------------------\n\nLIBRARY IEEE;\nUSE IEEE.STD_LOGIC_1164.ALL;\nuse IEEE.NUMERIC_STD.ALL;\n\nentity lba_ctrl is\n	port(\n    clk_i				    : in std_logic;\n	reset_i				    : in std_logic;\n	-- from DM3730 GPMC trough Local Bus\n	nCS3_LB_i				: in std_logic;\n	nADV_LB_i				: in std_logic;\n	nOE_LB_i				: in std_logic;\n	nWE_LB_i				: in std_logic;\n	Addr_LB_i				: in std_logic_vector(8 downto 0);\n    lba_nwait_o             : out std_logic;\n	-- from/to tri-state buffer on the top\n	lb_add_data_wr_i		: in std_logic_vector(15 downto 0);\n	lba_oe_o				: out std_logic;	-- lba_data_rd is connected directly to the LB data mux\n	-- from/to lba_std_interface and lba_usr_interface\n	lba_wr_en_o             : out std_logic;\n	lba_rd_en_o             : out std_logic;\n	lba_add_o               : out std_logic_vector(22 downto 0);\n	lba_cs_std_o       		: out std_logic; \n	lba_cs_usr_rd_o       	: out std_logic; \n    lba_cs_usr_wr_o       	: out std_logic; \n	lba_wait_usr_i    		: in std_logic\n	);\nend lba_ctrl;\n\narchitecture structural of lba_ctrl is\n\n \n\n\n\nsignal nCS3_LB_s        : std_logic;\nsignal nADV_LB_s        : std_logic;\nsignal nOE_LB_s         : std_logic;\nsignal nWE_LB_s	        : std_logic;\nsignal lba_wait_s       : std_logic;\nsignal lba_add_en_s : std_logic;\nsignal lb_add_s         : STD_LOGIC_VECTOR(22 downto 0);\n\n\n\n-- lfsm \n-- main FSM\n type state_fsm1_t is (\n    init,                       --  0\n    wait_cs_assertion,          --  1\n    Start_Read_Cycle,       --  2\n    check_wait_usr,  			--  3\n    send_data_usr_to_cpu,     	--  4\n    send_wait_usr_to_cpu,      	--  5 \n    enable_write_to_usr,      	--  6 \n    wait_end_of_acces_usr,   	--  7 		 \n	enable_write_to_std,  		--  8        \n	wait_end_of_acces_std,	    --  9\n    enable_read_from_std,       -- 10                 \n	send_data_std_to_cpu		-- 11\n  );\n  \n-- address FSM\n   type state_fsm2_t is (\n    init,                 --  0\n    get_address,          --  1\n    wait_cs_deassertion   --  2\n  );\n  \n  signal present_st_s, futur_st_s : state_fsm1_t;\n  signal psnt_st_s, fut_st_s : state_fsm2_t;\n  signal lba_cs_std_s       : std_logic;\n  signal lba_cs_usr_rd_s    : std_logic;\n  signal lba_cs_usr_wr_s    : std_logic;\n  signal lba_wr_en_s        : std_logic;\n  signal lba_rd_en_s        : std_logic;\n  signal lba_oe_s           : std_logic;\n  signal lba_wait_fsm_s	        : std_logic;\n  signal lba_add_en_fsm_s       : std_logic; \n\n\n\n\nbegin\n\n	input_synchro: process (clk_i, reset_i)\n	begin\n		if( reset_i = '1' ) then\n			nCS3_LB_s		 <= '1';\n            nADV_LB_s		 <= '1';\n            nOE_LB_s		 <= '1';\n            nWE_LB_s		 <= '1';	\n		elsif( Rising_Edge(clk_i) ) then      \n			nCS3_LB_s		 <= nCS3_LB_i;\n            nADV_LB_s		 <= nADV_LB_i;\n            nOE_LB_s		 <= nOE_LB_i;\n            nWE_LB_s		 <= nWE_LB_i;	\n		end if;\n	end process;\n\n\n	lba_nwait_o <= not lba_wait_s;\n	\n	address_register: process (clk_i, reset_i)\n	begin\n		if( reset_i = '1' ) then\n			lb_add_s <= (others => '0');\n		elsif( Rising_Edge(clk_i) ) then  \n			if lba_add_en_s = '1' then -- saves the address when it is valid\n				lb_add_s <= Addr_LB_i(6 downto 0) & lb_add_data_wr_i;			\n			end if;\n		end if;\n	end process;\n	\n	-- outputs\n	lba_add_o <= lb_add_s;\n    \n    \n    \n    \n    -- fsm\n---- main FSM -----------------------------------------------------------------------------------------------------------------------------------------------------------------------------------------\n  -- Futur state and outputs decoder\n  state_decoder : process (nCS3_LB_s, nOE_LB_s, nWE_LB_s, \n						Addr_LB_i(8 downto 7), lba_wait_usr_i,present_st_s) is\n\n  begin\n  \n    -- Default values\n    lba_cs_std_s 	<= '0';    \n    lba_cs_usr_wr_s <= '0';    \n    lba_cs_usr_rd_s <= '0'; \n    lba_wr_en_s  	<= '0';\n    lba_rd_en_s     <= '0';      \n    lba_oe_s       	<= '0';  \n    lba_wait_fsm_s		<= '0';\n    \n    -- State machine\n    case present_st_s is\n      when init =>\n              \n        -- ensure that nCS is inactive (the last access has finished)\n        if nCS3_LB_s = '1' then\n          futur_st_s <= wait_cs_assertion;\n        else\n          futur_st_s <= init;\n        end if;\n      \n      -- start of access\n      when wait_cs_assertion =>\n        -- read access to STD interface\n        if nCS3_LB_s = '0' AND Addr_LB_i(8 downto 7) = \"00\" AND nWE_LB_s = '1' AND nOE_LB_s = '0'  then\n          futur_st_s <= enable_read_from_std;\n		-- read access to USR interface  \n		elsif  nCS3_LB_s = '0' AND Addr_LB_i(8 downto 7) = \"01\" AND nWE_LB_s = '1' AND nOE_LB_s = '0'  then\n          futur_st_s <= Start_Read_Cycle; \n		-- write access to STD interface   \n		elsif  nCS3_LB_s = '0' AND Addr_LB_i(8 downto 7) = \"00\" AND nWE_LB_s = '0' AND nOE_LB_s = '1'  then\n          futur_st_s <= enable_write_to_std; \n		-- write access to USR interface   \n		elsif  nCS3_LB_s = '0' AND Addr_LB_i(8 downto 7) = \"01\" AND nWE_LB_s = '0' AND nOE_LB_s = '1'  then\n          futur_st_s <= enable_write_to_usr; \n        else\n          futur_st_s <= wait_cs_assertion;\n        end if;\n		\n ------------------------------------------------------------------\n-- READ from standard interface\n------------------------------------------------------------------\n       \n      when enable_read_from_std =>\n        lba_cs_std_s <= '1';   \n        lba_rd_en_s  <= '1';\n    \n        futur_st_s <= send_data_std_to_cpu;\n        \n     \n      when send_data_std_to_cpu =>\n\n        lba_cs_std_s <= '1'; \n		lba_rd_en_s  <= '1';\n        lba_oe_s     <= '1';  \n        \n        if nOE_LB_s = '1' then\n          futur_st_s <= init;\n        else\n          futur_st_s <= send_data_std_to_cpu;\n        end if;\n		\n  ------------------------------------------------------------------\n -- READ from user interface\n ------------------------------------------------------------------\n   \n      when Start_Read_Cycle =>\n        lba_cs_usr_rd_s <= '1';   \n        \n    \n        futur_st_s <= check_wait_usr;\n        \n   \n      when check_wait_usr =>\n        lba_cs_usr_rd_s <= '1';  \n		lba_rd_en_s  <= '1';\n                \n        -- data is not ready\n        if lba_wait_usr_i = '1' then\n          futur_st_s <= send_wait_usr_to_cpu; \n		-- data is ready  \n		else \n		  futur_st_s <= send_data_usr_to_cpu; \n        end if;\n      \n      when send_wait_usr_to_cpu =>\n        lba_cs_usr_rd_s <= '1';  \n		lba_rd_en_s  <= '1';\n        lba_wait_fsm_s	 <= '1';\n        \n        -- data is ready\n        if lba_wait_usr_i = '0' then\n          futur_st_s <= send_data_usr_to_cpu; \n		-- data is not ready  \n		else \n		  futur_st_s <= send_wait_usr_to_cpu; \n        end if;\n       \n        \n      when send_data_usr_to_cpu =>\n        lba_cs_usr_rd_s <= '1';   		\n        lba_oe_s	 <= '1';\n   \n        if nOE_LB_s = '1' then\n          futur_st_s <= init;\n        else\n          futur_st_s <= send_data_usr_to_cpu;\n        end if;\n ------------------------------------------------------------------\n -- WRITE to STD interface\n ------------------------------------------------------------------\n       \n      when enable_write_to_std =>\n        lba_cs_std_s <= '1';   \n        lba_wr_en_s  <= '1';\n    \n        futur_st_s <= init;\n        \n      \n      when wait_end_of_acces_std =>\n\n        lba_cs_std_s <= '1'; \n        \n        futur_st_s <= init;\n ------------------------------------------------------------------\n -- WRITE to USR interface\n ------------------------------------------------------------------\n      when enable_write_to_usr =>\n        lba_cs_usr_wr_s     <= '1';   \n        lba_wr_en_s         <= '1';\n    \n        futur_st_s <= init;\n        \n      \n    --  when wait_end_of_acces_usr =>\n\n      --  lba_cs_usr_s <= '1'; \n        \n       -- futur_st_s <= init;\n		\n	  when others =>\n	  \n	   futur_st_s <= init;\n	\n	end case;	\n  \n  end process state_decoder;\n  \n  \n  -- Synchronous\n  sequential : process (clk_i, reset_i)\n  \n  begin\n    if( reset_i = '1' ) then\n      present_st_s <= init;         \n    elsif( Rising_Edge(clk_i) ) then      \n      -- Save state\n      present_st_s <= futur_st_s;\n    end if;\n  end process sequential;\n  \n---- end of main FSM -----------------------------------------------------------------------------------------------------------------------------------------------------------------------------------------\n  \n---- address FSM -----------------------------------------------------------------------------------------------------------------------------------------------------------------------------------------\n  state_decoder2 : process (nCS3_LB_s, nADV_LB_s,psnt_st_s) is\n\n  begin\n  \n    -- Default values\n    lba_add_en_fsm_s <= '0';\n    \n    -- State machine\n    case psnt_st_s is\n	\n      when init =>\n              \n        if nCS3_LB_s = '0' AND nADV_LB_s = '0' then\n          fut_st_s <= get_address;\n        else\n          fut_st_s <= init;\n        end if;\n		\n	  when get_address =>\n	  \n	    lba_add_en_fsm_s <= '1';\n              \n        fut_st_s <= wait_cs_deassertion;\n		\n      when wait_cs_deassertion =>\n              \n        if nCS3_LB_s = '1' then\n          fut_st_s <= init;\n        else\n          fut_st_s <= wait_cs_deassertion;\n        end if;\n	  \n	  when others => \n	    fut_st_s <= wait_cs_deassertion;\n		\n	end case;\n  end process state_decoder2;\n  \n  -- Synchronous\n  memory : process (clk_i, reset_i)\n  \n  begin\n    if( reset_i = '1' ) then\n      psnt_st_s <= init;         \n    elsif( Rising_Edge(clk_i) ) then      \n      -- Save state\n      psnt_st_s <= fut_st_s;\n    end if;\n  end process memory;\n  \n  \n---- end of address FSM -----------------------------------------------------------------------------------------------------------------------------------------------------------------------------------------\n\n  -- outputs \n  lba_cs_std_o      <= lba_cs_std_s;\n  lba_cs_usr_rd_o   <= lba_cs_usr_rd_s;\n  lba_cs_usr_wr_o   <= lba_cs_usr_wr_s;\n  lba_wr_en_o       <= lba_wr_en_s ;\n  lba_rd_en_o       <= lba_rd_en_s; \n  lba_oe_o          <= lba_oe_s;    \n  lba_wait_s        <= lba_wait_fsm_s;	\n  lba_add_en_s      <= lba_add_en_fsm_s;    \n  \nend structural;")) lba_ctrl_1: pin names not known; wires that end beside it: clk, Reset, reptarlb_1_p1, reptarlb_1_p2, reptarlb_1_p3, reptarlb_1_p4, reptarlb_1_p9, reptarlb_1_p6, lba_ctrl_1_p9, lba_ctrl_1_p10, lba_ctrl_1_p11, lba_ctrl_1_p12, lba_ctrl_1_p13, lba_ctrl_1_p14, lba_ctrl_1_p15, lba_ctrl_1_p16, lba_ctrl_1_p17
  Button SW6 (.out(Switchs[5]));
  Button SW7 (.out(Switchs[6]));
  Button SW1 (.out(Switchs[0]));
  Button SW2 (.out(Switchs[1]));
  Button SW5 (.out(Switchs[4]));
  Button SW3 (.out(Switchs[2]));
  Button SW8 (.out(Switchs[7]));
  Button SW4 (.out(Switchs[3]));
  mux_lba_data_select mux_lba_data_select_1 (
    .cs_usr_rd_i(lba_ctrl_1_p16), .cs_usr_wr_i(lba_ctrl_1_p17), .cs_std_i(lba_ctrl_1_p15),
    .data_usr_i(l_lba_user_interface_data_rd_o), .data_std_i(lba_std_interface_p10), .data_o(reptarlb_1_p7));
  _7_Segment_Display Aff_7seg_3 (.dp(Switchs[4]));  // open: g, f, a, b, e, d, c
  lba_user_interface l_lba_user_interface (
    .Leds_o(Leds), .aff_7seg_o(aff_7seg_1), .IRQ_user_o(reptarlb_1_p10), .wait_user_o(lba_ctrl_1_p9),
    .data_rd_o(l_lba_user_interface_data_rd_o), .switchs_i(Switchs), .addr_i(lba_ctrl_1_p14),
    .data_wr_i(reptarlb_1_p6), .reset(Reset), .clk(clk), .cs_rd_i(lba_ctrl_1_p16), .rd_en_i(lba_ctrl_1_p13),
    .wr_en_i(lba_ctrl_1_p12), .cs_wr_i(lba_ctrl_1_p17));
  // VHDL_Entity #(.content("------------------------------------------------------------------------------------------\n-- HEIG-VD ///////////////////////////////////////////////////////////////////////////////\n-- Haute Ecole d'Ingenerie et de Gestion du Canton de Vaud\n-- School of Business and Engineering in Canton de Vaud\n------------------------------------------------------------------------------------------\n-- REDS Institute ////////////////////////////////////////////////////////////////////////\n-- Reconfigurable Embedded Digital Systems\n------------------------------------------------------------------------------------------\n--\n-- File                 : lba_sp6_registers.vhd\n-- Author               : Evangelina Lolivier-Exler\n-- Date                 : 24.10.2013\n-- Target Devices       : Spartan6 xc6slx150t-3fgg900\n--\n-- Context              : Reptar - FPGA design\n--\n---------------------------------------------------------------------------------------------\n-- Description :		Address decoder and registers for CPU access to the REPTAR peripherals\n--						The registers contained in this block are described in the document \n--						Spartan6_registers.xlsx, tab \"Summary_Layout_v2_prop\"\n---------------------------------------------------------------------------------------------\n-- Information :\n---------------------------------------------------------------------------------------------\n-- Modifications :\n-- Ver   Date        Engineer     Comments\n-- 0.0   See header  ELR          Initial version, based on Reptar_local_bus_v2.vhd of VTT\n-- 0.1   10.01.14	 ELR		  The bit IRQ_CTL_REG_s(0) is driven by a State Machine instead \n--								  of the write process in order to implement the hardware reset \n--								  feature for this bit\n-- 0.2   23.01.14    ELR		  GPIO_H_OE_REG added in the read process. Read process splitted in two\n-- 0.3   28.01.14    CVZ          added IRQ_enable signal\n---------------------------------------------------------------------------------------------\nlibrary ieee;\n  use ieee.std_logic_1164.all;\n  --use ieee.numeric_std.all;\n\nentity lba_sp6_registers is\n  port(\n  -------------------------------------------------------------------------\n  --Insert input ports below  \n    clk_i  : in  std_logic;                    -- input bit example\n    reset_i: in std_logic;\n    --lba_data_wr_i      : in  std_logic_vector(15 downto 0);\n    lba_cs_std_i	  : in std_logic;\n    lba_rd_en_i       : in std_logic;\n    lba_add_i		  : in std_logic_vector(22 downto 0);\n    HW_VERSION_i 	  : in std_logic_vector(3 downto 0);\n    ID_DESIGN_FPGA_i  : in std_logic_vector(8 downto 0);\n    ID_SUB_DESIGN_i   : in std_logic_vector(7 downto 0);\n    VERSION_NUMBER_i  : in std_logic_vector(7 downto 0);\n    \n  -------------------------------------------------------------------------\n  --Insert output ports below  \n    lba_data_rd_std_o : out std_logic_vector(15 downto 0)\n\n    );\nend lba_sp6_registers;\n\n---------------------------------------------------------------------------\n--Complete your VHDL description below\narchitecture type_architecture of lba_sp6_registers is \n 	constant ID_FPGA_c              : std_logic_vector (2 downto 0):= \"001\"; -- 000 Spartan3, 001 Spartan6\n	constant	VERSION1_REG_ADD_c		  		: std_logic_vector(15 downto 0) := x\"00_00\"; --0x0000 RW\n	constant	VERSION2_REG_ADD_c		  		: std_logic_vector(15 downto 0) := x\"00_01\"; --0x0002 RW\n	\n	signal	VERSION1_REG_s		  	: std_logic_vector(15 downto 0); \n	signal	VERSION2_REG_s		  	: std_logic_vector(15 downto 0); \n  	signal 	read_en_s				: std_logic;\n  	signal 	data_in_s				: std_logic_vector(15 downto 0);\n  \nbegin\n	read_en_s <= lba_rd_en_i and lba_cs_std_i;\n	--data_in_s <= lba_data_wr_i;\n	VERSION1_REG_s		<= HW_version_i & ID_FPGA_c & ID_DESIGN_FPGA_i; \n	VERSION2_REG_s		<= ID_SUB_DESIGN_i & VERSION_NUMBER_i; \n	\n\n\n-- Read process\n	process(clk_i, reset_i)\n	begin\n	if(reset_i='1') then\n		lba_data_rd_std_o <=  x\"00_00\";\n	elsif rising_edge(clk_i) then\n		if read_en_s = '1' and lba_add_i(22 downto 16) = \"0000000\"  then\n			case lba_add_i(15 downto 0) is\n				when VERSION1_REG_ADD_c =>\n					lba_data_rd_std_o <=VERSION1_REG_s;\n				when VERSION2_REG_ADD_c =>\n					lba_data_rd_std_o  <= VERSION2_REG_s;\n				when others	=> \n					lba_data_rd_std_o <=  x\"00_00\";\n			end case;\n		end if;\n	end if;\nend process;\n\nend type_architecture;")) lba_std_interface: pin names not known; wires that end beside it: clk, Reset, lba_ctrl_1_p15, lba_ctrl_1_p13, lba_ctrl_1_p14, 4'b0010, 9'h3, {8{1'b0}}, {8{1'b0}}, lba_std_interface_p10
  _7_Segment_Display u_Aff_7seg_1 (
    .g(aff_7seg_1[6]), .f(aff_7seg_1[5]), .a(aff_7seg_1[0]), .b(aff_7seg_1[1]), .e(aff_7seg_1[4]),
    .d(aff_7seg_1[3]), .c(aff_7seg_1[2]), .dp(aff_7seg_1[7]));
  LED LED0 (.in(Leds[0]));
  LED LED1 (.in(Leds[1]));
  LED LED2 (.in(Leds[2]));
  LED LED3 (.in(Leds[3]));
  LED LED4 (.in(Leds[4]));
  LED LED5 (.in(Leds[5]));
  LED LED6 (.in(Leds[6]));
  LED LED7 (.in(Leds[7]));

  // Notes on the sheet:
  //   Attention, votre version de Logisim
  //   ne contient pas de tracker. Si vous
  //   enregistrez votre projet, toutes les
  //   informations du tracker seront
  //   définitivement effacées.
  //   user interface 0x19000000
  //   std interface: 0x18000000
endmodule

module lba_user_interface (
  input  reset,
  input  clk,
  input  cs_rd_i,
  input  rd_en_i,
  input  wr_en_i,
  input  cs_wr_i,
  input  [22:0] addr_i,
  input  [15:0] data_wr_i,
  input  [7:0] switchs_i,
  output IRQ_user_o,
  output wait_user_o,
  output [7:0] Leds_o,
  output [7:0] aff_7seg_o,
  output [15:0] data_rd_o
);

  wire undriven_2;
  wire [2:0] user_addr_dec_1_sel_zone_addr_o;
  wire [15:0] multiplexer_1_out, undriven;

  user_addr_dec user_addr_dec_1 (
    .cs_wr_i(cs_wr_i), .wr_en_i(wr_en_i), .cs_rd_i(cs_rd_i), .adrr_i(addr_i),
    .sel_zone_addr_o(user_addr_dec_1_sel_zone_addr_o));  // open: cs_rd_zone_o, cs_led_o, cs_sw, cs_7seg1
  Multiplexer #(.select(3), .width(16)) multiplexer_1 (
    .in0(undriven), .out(multiplexer_1_out), .sel(user_addr_dec_1_sel_zone_addr_o), .en(undriven_2));  // open: in1, in2, in3, in4, in5, in6, in7
  Register #(.width(16)) register_1 (.D(multiplexer_1_out), .en(rd_en_i), .clk(clk), .Q(data_rd_o), .clr(reset));

  assign IRQ_user_o = 1'b0;
  assign wait_user_o = 1'b0;

  // Other names for the same wires on the sheet: rd_en = rd_en_i

  // Notes on the sheet:
  //   Attention, votre version de Logisim
  //   ne contient pas de tracker. Si vous
  //   enregistrez votre projet, toutes les
  //   informations du tracker seront
  //   définitivement effacées.
  //   val cst a definir !
  //   leds_value
  //   aff_7seg
  //   EN à compléter
endmodule

module mux_lba_data_select (
  input  cs_usr_rd_i,
  input  cs_usr_wr_i,
  input  cs_std_i,
  input  [15:0] data_usr_i,
  input  [15:0] data_std_i,
  output [15:0] data_o
);

  wire [0:0] or_1_out;

  or or_1 (or_1_out[0], cs_usr_rd_i, cs_usr_wr_i);
  Multiplexer #(.select(2), .width(16), .enable("false")) multiplexer_1 (
    .in0({16{1'b1}}), .in1(data_usr_i), .in2(data_std_i), .in3({16{1'b1}}), .out(data_o),
    .sel({cs_std_i, or_1_out[0]}));

  // Notes on the sheet:
  //   Attention, votre version de Logisim
  //   ne contient pas de tracker. Si vous
  //   enregistrez votre projet, toutes les
  //   informations du tracker seront
  //   définitivement effacées.
  //   mux_lba_data_select: effectue la sélection entre les data de std interface et user interface.
endmodule

module user_addr_dec (
  input  cs_wr_i,
  input  wr_en_i,
  input  cs_rd_i,
  input  [22:0] adrr_i,
  output cs_rd_zone_o,
  output [2:0] sel_zone_addr_o,
  output cs_led_o,
  output cs_sw,
  output cs_7seg1
);

  wire comparator_1_eq, undriven;

  Comparator #(.width(20), .mode("unsigned")) comparator_1 (
    .a({20{1'b0}}), .b(adrr_i[22:3]), .eq(comparator_1_eq));  // open: gt, lt
  Decoder #(.select(3)) decoder_1 (
    .sel(adrr_i[2:0]), .en(comparator_1_eq));  // open: out0, out1, out2, out3, out4, out5, out6, out7
  and and_1 (cs_rd_zone_o, undriven, comparator_1_eq);

  assign sel_zone_addr_o = adrr_i[2:0];

  // Other names for the same wires on the sheet: wr_en = wr_en_i

  // Notes on the sheet:
  //   Attention, votre version de Logisim
  //   ne contient pas de tracker. Si vous
  //   enregistrez votre projet, toutes les
  //   informations du tracker seront
  //   définitivement effacées.
  //   Adresse de la plage !
  //   A compléter !
  //   A compléter !
  //   A compléter !
  //   Completer liste cs ....
endmodule
